// Digital circuit memory_controller.dig as structural Verilog
module memory_controller (
  input  clk,
  input  [15:0] addr_in,
  input  [3:0] SPI_in,
  input  rst,
  input  [7:0] data_in,
  input  write,
  input  sel_flash,
  input  sel_ram,
  output [7:0] data_out,
  output data_ready,
  output [3:0] SPI_out,
  output SPI_oe,
  output SPI_csflash,
  output SPI_csram
);

  wire and_4_out, comparator_1_eq, comparator_3_eq, comparator_4_eq, comparator_5_lt, comparator_6_eq,
       comparator_7_eq, or_1_out, or_3_out, or_4_out, or_5_out, readdata, ready_w, writedata;
  wire [3:0] multiplexer_3_out, state;
  wire [7:0] cmd;

  or or_1 (or_1_out, rst, data_ready, ready_w);
  Counter #(.Bits(4)) counter_1 (.en(1'b1), .C(clk), .clr(or_1_out), .out(state));  // open: ovf
  Multiplexer #(.Bits(8)) multiplexer_1 (.sel(write), .in_0(8'hb), .in_1(8'h2), .out(cmd));
  Multiplexer #(.Selector_Bits(4), .Bits(4)) multiplexer_2 (
    .sel(state), .in_0(4'b0000), .in_1(cmd[7:4]), .in_2(cmd[3:0]), .in_3({1'b0, addr_in[14:12]}),
    .in_4(addr_in[11:8]), .in_5(addr_in[7:4]), .in_6(addr_in[3:0]), .in_7(4'b0000), .in_8(4'b0000),
    .in_9(data_in[7:4]), .in_10(data_in[3:0]), .in_11(4'b0000), .in_12(4'b0000), .in_13(4'b0000),
    .in_14(4'b0000), .in_15(4'b0000), .out(SPI_out));
  Comparator #(.Bits(4)) comparator_1 (.a(4'b1101), .b(state), .eq(comparator_1_eq));  // open: gt, lt
  Comparator #(.Bits(4)) comparator_2 (.a(4'b1110), .b(state), .eq(data_ready));  // open: gt, lt
  Comparator #(.Bits(4)) comparator_3 (.a(state), .b(4'b1001), .eq(comparator_3_eq));  // open: gt, lt
  Comparator #(.Bits(4)) comparator_4 (.a(state), .b(4'b1010), .eq(comparator_4_eq));  // open: gt, lt
  Comparator #(.Bits(4)) comparator_5 (.a(state), .b(4'b1010), .lt(comparator_5_lt));  // open: gt, eq
  or or_2 (readdata, comparator_1_eq, data_ready);
  or or_3 (or_3_out, comparator_3_eq, comparator_4_eq);
  and and_1 (ready_w, comparator_4_eq, write);
  or or_4 (or_4_out, comparator_5_lt, writedata);
  Comparator #(.Bits(4)) comparator_6 (.a(state), .b(4'b0000), .eq(comparator_6_eq));  // open: gt, lt
  Comparator #(.Bits(4)) comparator_7 (.a(state), .b(4'b0001), .eq(comparator_7_eq));  // open: gt, lt
  Multiplexer #(.Bits(4)) multiplexer_3 (
    .sel(data_ready), .in_0(SPI_in), .in_1(data_out[3:0]), .out(multiplexer_3_out));
  and and_2 (writedata, or_3_out, write);
  or or_5 (or_5_out, comparator_6_eq, comparator_7_eq);
  and and_3 (SPI_oe, or_4_out, ~rst);  // And
  and and_4 (and_4_out, ~rst, ~or_5_out);  // And
  Register #(.Bits(8)) register_1 (.D({SPI_in, multiplexer_3_out}), .C(clk), .en(readdata), .Q(data_out));
  and and_5 (SPI_csram, sel_ram, and_4_out);
  and and_6 (SPI_csflash, and_4_out, sel_flash);

  // Other names for the same wires on the sheet: addr[15:0] = addr_in; ready_r = data_ready

  // Notes on the sheet:
  //   SPI_out: Output
endmodule
