// Digital circuit nna8v2_mpu_mux.dig as structural Verilog
module nna8v2_mpu_mux (
  input  clk,
  input  [7:0] data_in,
  input  rst,
  output [15:0] addr_out,
  output [7:0] data_out,
  output r,
  output w,
  output brk
);

  wire add_carry, and_3_out, and_6_out, and_7_out, and_8_out, and_14_out, and_18_out, and_19_out, and_20_out,
       and_21_out, and_24_out, and_25_out, and_26_out, bra, cal, cal_flag, co_add, co_sub, comparator_1_eq,
       comparator_1_lt, d_ff_1_nq, dec, dec_flag, decoder_2_out_0, decoder_2_out_1, decoder_3_out_0,
       decoder_3_out_1, decoder_3_out_2, decoder_3_out_3, decoder_4_out_0, decoder_4_out_1, decoder_4_out_2,
       decoder_4_out_3, eq, eq_flag, flag_out, flg, flg_flag, gt, gt_flag, inc, inc_flag, jmp, lih, lil, mco,
       mdb, memr, memrw, mov, mpb, mrd, multiplexer_7_out, mwr, nclock, nop, not_1_out, not_2_out, not_3_out,
       not_4_out, not_6_out, or_1_out, or_5_out, or_7_out, or_8_out, or_9_out, or_10_out, or_11_out,
       or_12_out, or_13_out, or_14_out, or_15_out, or_16_out, or_18_out, pc_write, reg_we, sin, sub_carry,
       xcycle, xcycle_next, \xor ;
  wire [1:0] selreg;
  wire [3:0] arg, co, curop, lih_rslt;
  wire [7:0] add_rslt, and_4_out, and_5_out, and_rslt, cal_rslt, data_in_t, db, dec_rslt, inc_rslt,
       memrw_addr, mul_rslt, not_rslt, or_rslt, pb, pc, pc_next, r1_q, r2_q, r3_q, regin, sub_rslt, xor_rslt;
  wire [7:4] lil_rslt;
  wire [15:8] mul_1_mul;

  or or_1 (or_1_out, jmp, bra);
  or or_2 (memrw, w, memr);
  and and_1 (w, xcycle, mwr);
  and and_2 (memr, xcycle, mrd);
  and and_3 (and_3_out, or_1_out, ~flag_out);  // And
  assign and_4_out = data_out & {8{jmp}};  // And and_4, 8 bits wide
  assign and_5_out = {pc[7:4], arg} & {8{bra}};  // And and_5, 8 bits wide
  assign pc_next = and_4_out | and_5_out;  // Or or_3, 8 bits wide
  or or_4 (pc_write, and_3_out, rst);
  not not_1 (not_1_out, xcycle);
  or or_5 (or_5_out, rst, not_1_out);
  // Probe on arg[3:2]
  // Probe on arg[1:0]
  Register #(.Bits(8)) u_curop (.D(data_in_t), .C(clk), .en(or_5_out), .Q({curop, arg}));
  Decoder #(.Selector_Bits(4)) decoder_1 (
    .sel(curop), .out_0(sin), .out_1(eq), .out_2(gt), .out_3(flg), .out_5(bra), .out_6(mco), .out_7(mwr),
    .out_8(mrd), .out_9(lil), .out_10(lih), .out_11(mov), .out_12(cal), .out_13(\xor ), .out_14(inc),
    .out_15(dec));  // open: out_4
  // Probe on curop
  // Probe on arg
  and and_6 (and_6_out, not_2_out, not_3_out);
  not not_2 (not_2_out, flag_out);
  not not_3 (not_3_out, arg[2]);
  and and_7 (and_7_out, arg[3], arg[2]);
  Decoder #(.Selector_Bits(2)) decoder_2 (
    .sel(arg[3:2]), .out_0(decoder_2_out_0), .out_1(decoder_2_out_1));  // open: out_2, out_3
  Decoder #(.Selector_Bits(2)) decoder_3 (
    .sel(arg[1:0]), .out_0(decoder_3_out_0), .out_1(decoder_3_out_1), .out_2(decoder_3_out_2),
    .out_3(decoder_3_out_3));
  and and_8 (and_8_out, sin, decoder_3_out_0);
  or or_6 (flg_flag, and_6_out, and_7_out);
  and and_9 (nop, and_8_out, decoder_2_out_0);
  and and_10 (brk, and_8_out, decoder_2_out_1);
  and and_11 (jmp, decoder_3_out_1, sin);
  and and_12 (mpb, decoder_3_out_2, sin);
  and and_13 (mdb, decoder_3_out_3, sin);
  and and_14 (and_14_out, ~xcycle, mrd);  // And
  or or_7 (or_7_out, lil, lih);
  and and_15 (reg_we, curop[3], ~and_14_out);  // And
  and and_16 (selreg[1], arg[3], ~or_7_out);  // And
  and and_17 (selreg[0], arg[2], ~or_7_out);  // And
  Multiplexer #(.Selector_Bits(4), .Bits(8)) multiplexer_1 (
    .sel(curop), .in_0({8{1'b0}}), .in_1({8{1'b0}}), .in_2({8{1'b0}}), .in_3({8{1'b0}}), .in_4({8{1'b0}}),
    .in_5({8{1'b0}}), .in_6({8{1'b0}}), .in_7({8{1'b0}}), .in_8(data_in_t), .in_9({lil_rslt, arg}),
    .in_10({arg, lih_rslt}), .in_11(memrw_addr), .in_12(cal_rslt), .in_13(xor_rslt), .in_14(inc_rslt),
    .in_15(dec_rslt), .out(regin));
  Decoder #(.Selector_Bits(2)) decoder_4 (
    .sel(selreg), .out_0(decoder_4_out_0), .out_1(decoder_4_out_1), .out_2(decoder_4_out_2),
    .out_3(decoder_4_out_3));
  Multiplexer #(.Bits(8)) multiplexer_2 (.sel(not_4_out), .in_0(db), .in_1(pb), .out(addr_out[15:8]));
  not not_4 (not_4_out, memrw);
  not not_5 (nclock, clk);
  or or_8 (or_8_out, pc_write, rst);
  and and_18 (and_18_out, decoder_4_out_0, reg_we);
  and and_19 (and_19_out, decoder_4_out_1, reg_we);
  and and_20 (and_20_out, decoder_4_out_2, reg_we);
  and and_21 (and_21_out, decoder_4_out_3, reg_we);
  assign data_in_t = data_in & ~{8{rst}};  // And and_22, 8 bits wide
  or or_9 (or_9_out, and_18_out, rst);
  or or_10 (or_10_out, and_19_out, rst);
  or or_11 (or_11_out, and_20_out, rst);
  or or_12 (or_12_out, and_21_out, rst);
  or or_13 (or_13_out, rst, mpb);
  or or_14 (or_14_out, rst, mdb);
  or or_15 (or_15_out, rst, mco);
  CounterPreset #(.Bits(8), .isProgramCounter("true")) u_PC (
    .en(~xcycle), .C(clk), .dir(1'b0), .in(pc_next), .ld(or_8_out), .clr(mpb), .out(pc));  // open: ovf
  or or_16 (or_16_out, mrd, pc_write, mwr);
  Register #(.Bits(8)) r0 (.D(regin), .C(nclock), .en(or_9_out), .Q({lil_rslt, lih_rslt}));
  Register #(.Bits(8)) r1 (.D(regin), .C(nclock), .en(or_10_out), .Q(r1_q));
  Register #(.Bits(8)) r2 (.D(regin), .C(nclock), .en(or_11_out), .Q(r2_q));
  Register #(.Bits(8)) r3 (.D(regin), .C(nclock), .en(or_12_out), .Q(r3_q));
  Register #(.Bits(8)) u_pb (.D(data_out), .C(nclock), .en(or_13_out), .Q(pb));
  Register #(.Bits(8)) u_db (.D(data_out), .C(nclock), .en(or_14_out), .Q(db));
  Register #(.Bits(4)) u_co (.D(arg), .C(nclock), .en(or_15_out), .Q(co));
  or or_17 (r, memr, ~xcycle);  // Or
  and and_23 (xcycle_next, d_ff_1_nq, or_16_out);
  // Probe on {lil_rslt, lih_rslt}
  // Probe on r1_q
  // Probe on r2_q
  // Probe on r3_q
  // Probe on pb
  Break u_mpb (.brk(or_13_out));
  // Probe on db
  Break u_mdb (.brk(or_14_out));
  // Probe on co
  D_FF d_ff_1 (.D(xcycle_next), .C(~clk), .Q(xcycle), .nQ(d_ff_1_nq));
  Multiplexer #(.Selector_Bits(2), .Bits(8)) multiplexer_3 (
    .sel(arg[3:2]), .in_0({lil_rslt, lih_rslt}), .in_1(r1_q), .in_2(r2_q), .in_3(r3_q), .out(data_out));
  Multiplexer #(.Selector_Bits(2), .Bits(8)) multiplexer_4 (
    .sel(arg[1:0]), .in_0({lil_rslt, lih_rslt}), .in_1(r1_q), .in_2(r2_q), .in_3(r3_q), .out(memrw_addr));
  Multiplexer #(.Bits(8)) multiplexer_5 (.sel(xcycle), .in_0(pc), .in_1(memrw_addr), .out(addr_out[7:0]));
  // Probe on xcycle
  Add #(.Bits(8)) add_1 (.a(data_out), .b({{6{1'b0}}, arg[1:0]}), .c_i(1'b1), .s(inc_rslt), .c_o(inc_flag));
  Sub #(.Bits(8)) sub_1 (.a(data_out), .b({{6{1'b0}}, arg[1:0]}), .c_i(1'b1), .s(dec_rslt), .c_o(dec_flag));
  assign xor_rslt = data_out ^ memrw_addr;  // XOr xor_1, 8 bits wide
  Multiplexer #(.Selector_Bits(4), .Bits(8)) multiplexer_6 (
    .sel(co), .in_0(add_rslt), .in_1(sub_rslt), .in_2(mul_rslt), .in_3({8{1'b0}}), .in_4({8{1'b0}}),
    .in_5({8{1'b0}}), .in_6({8{1'b0}}), .in_7({8{1'b0}}), .in_8(and_rslt), .in_9(or_rslt), .in_10(not_rslt),
    .in_11({8{1'b0}}), .in_12({8{1'b0}}), .in_13({8{1'b0}}), .in_14({8{1'b0}}), .in_15({8{1'b0}}),
    .out(cal_rslt));
  Add #(.Bits(8)) add_2 (.a(data_out), .b(memrw_addr), .c_i(flag_out), .s(add_rslt), .c_o(add_carry));
  Sub #(.Bits(8)) sub_2 (.a(data_out), .b(memrw_addr), .c_i(flag_out), .s(sub_rslt), .c_o(sub_carry));
  Mul #(.Bits(8)) mul_1 (.a(data_out), .b(memrw_addr), .mul({mul_1_mul, mul_rslt}));
  Multiplexer #(.Selector_Bits(4)) multiplexer_7 (
    .sel(curop), .in_0(flag_out), .in_1(eq_flag), .in_2(gt_flag), .in_3(flg_flag), .in_4(flag_out),
    .in_5(flag_out), .in_6(flag_out), .in_7(flag_out), .in_8(flag_out), .in_9(flag_out), .in_10(flag_out),
    .in_11(flag_out), .in_12(cal_flag), .in_13(flag_out), .in_14(inc_flag), .in_15(dec_flag),
    .out(multiplexer_7_out));
  Decoder #(.Selector_Bits(4)) decoder_5 (
    .sel(co), .out_0(co_add), .out_1(co_sub));  // open: out_2, out_3, out_4, out_5, out_6, out_7, out_8, out_9, out_10, out_11, out_12, out_13, out_14, out_15
  not not_6 (not_6_out, clk);
  Register flag (.D(multiplexer_7_out), .C(not_6_out), .en(1'b1), .Q(flag_out));
  Comparator #(.Bits(8)) comparator_1 (
    .a(data_out), .b(memrw_addr), .eq(comparator_1_eq), .lt(comparator_1_lt));  // open: gt
  not not_7 (eq_flag, comparator_1_eq);
  not not_8 (gt_flag, comparator_1_lt);
  or or_18 (or_18_out, co_add, co_sub);
  and and_24 (and_24_out, co_add, add_carry);
  and and_25 (and_25_out, co_sub, sub_carry);
  and and_26 (and_26_out, ~or_18_out, flag_out);  // And
  assign and_rslt = data_out & memrw_addr;  // And and_27, 8 bits wide
  assign or_rslt = data_out | memrw_addr;  // Or or_19, 8 bits wide
  assign not_rslt = ~data_out;  // Not not_9, 8 bits wide
  or or_20 (cal_flag, and_24_out, and_25_out, and_26_out);

  // Other names for the same wires on the sheet: arg1[1:0] = arg[1:0]; lih_rslt[7:4] = arg; lil_rslt[3:0] = arg;
  //   arg0[1:0] = arg[3:2]; addr[7:0] = addr_out[7:0]; bank[7:0] = addr_out[15:8]; clock = clk; memw = w;
  //   mrd_rslt[7:0] = data_in_t; mwr_rslt[7:0] = data_out; regout_arg0[7:0] = data_out; mov_rslt[7:0] = memrw_addr;
  //   regout_arg1[7:0] = memrw_addr; regout_r0[7:0] = {lil_rslt, lih_rslt}; reset = rst

  // Notes on the sheet:
  //   clk: Hz: 2000
  //   data_out: byte to be written
  //   r: The cpu wants to read the value at the address addr_out into data_in
  //   w: The cpu wants to write the value of data_out to the address addr_out
  //   rst: Reset the processor
  //   operations
  //   jmp bra
  //   mwr, mrd
  //   op decoder
  //   mov
  //   flg
  //   lil lih
  //   sin
  //   registers
  //   for mrd instruction only set reg_we on the xcylce
  //   select r0 on lil,lih ops
  //   memory
  //   IO
  //   pc,clock
  //   alu
  //   inc dec xor
  //   cal
  //   flag
  //   arithmetic
  //   shifts
  //   flag ctrl
  //   logical
endmodule
